# Fritzing sketch tagger (saved by Fritzing 0.9.3b)

parts:
  U1 = ESP32S-HiLetgo [part_number=ESP32S-HiLetgo]
  S1 = Momentary Switch [package=ksa_sealed_tac_switch]
  IR1 = TSOP312.., 314.. [package=THT]
  R1 = Resistor [tolerance=±5% resistance=10 package=THT]
  LED1 = LEDs [package=led10mm]
  Bauteil1 = ws2812b [package=THT]

nets:
  N1: U1.3.3, IR1.Vs
  N2: U1.GPIO27, IR1.Data
  GND: U1.GND, S1.3, IR1.GND, LED1.A, Bauteil1.VSS
  VIN: U1.VIN, Bauteil1.VDD
  N3: U1.GPIO19, Bauteil1.DIN
  N4: U1.GPIO21, S1.1
  N5: U1.GPIO22, R1.Pin_0
  N6: R1.Pin_1, LED1.C

custom parts:
  ESP32S-HiLetgo: HiLetgo ESP-WROOM-32 ESP32 ESP-32S Development Board 2.4GHz Dual-Mode WiFi + Bluetooth Dual Cores Microcontroller The ESP32 integrated with Antenna switches, RF Balun, power amplifiers, low-noise amplifiers, filters, and management modules, and the entire solution occupies the least area of PCB. 2.4 GHz Wi-Fi plus Bluetooth dual-mode chip, with TSMC Ultra-low power consumption 40nm technology,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
